// Logisim project PROJETO1.circ as structural Verilog: 7 circuits, main circuit PROJETO
module PROJETO (
  input  [7:0] A,
  input  [7:0] B,
  input  [2:0] in_3,
  input  [2:0] in_4,
  input  Cin1,
  input  Cin2,
  input  [3:0] OP,
  output [7:0] S
);

  wire [7:0] and_1_out, nor_1_out, or_1_out, shifter_1_out, shifter_2_out, somador_8bits_1_s,
       subtrator_8bits_1_s, xor_1_out;

  Shifter shifter_1 (.in(B), .\dist (in_3), .out(shifter_1_out));
  Shifter #(.shift("lr")) shifter_2 (.in(B), .\dist (in_4), .out(shifter_2_out));
  assign and_1_out = A & B;  // AND_Gate and_1, 8 bits wide
  assign or_1_out = A | B;  // OR_Gate or_1, 8 bits wide
  assign xor_1_out = A ^ B;  // XOR_Gate xor_1, 8 bits wide
  assign nor_1_out = ~(A | B);  // NOR_Gate nor_1, 8 bits wide
  SOMADOR_8BITS somador_8bits_1 (.S(somador_8bits_1_s), .A(A), .B(B), .Cin(Cin1));  // open: Cout
  SUBTRATOR_8BITS subtrator_8bits_1 (.S(subtrator_8bits_1_s), .A(A), .B(B), .Cin(Cin2));  // open: Cout
  Multiplexer #(.select(4), .width(8), .enable("false")) multiplexer_1 (
    .in0(somador_8bits_1_s), .in1(shifter_1_out), .in2({8{1'b0}}), .in3(shifter_2_out),
    .in4(subtrator_8bits_1_s), .in5({8{1'b0}}), .in6(and_1_out), .in7(or_1_out), .in8({8{1'b0}}),
    .in9({8{1'b0}}), .in10({8{1'b0}}), .in11(xor_1_out), .in12({8{1'b0}}), .in13({8{1'b0}}),
    .in14(nor_1_out), .in15({8{1'b0}}), .out(S), .sel(OP));

  // Notes on the sheet:
  //   CinSOM
  //   CinSUB
endmodule

module MEIO_SOMADOR (
  input  A,
  input  B,
  output S,
  output Cout
);

  xor xor_1 (S, A, B);
  and and_1 (Cout, B, A);
endmodule

module MEIO_SUBTRATOR (
  input  A,
  input  B,
  output S,
  output Tout
);

  xor xor_1 (S, A, B);
  and and_1 (Tout, B, ~A);  // AND_Gate
endmodule

module SOMADOR_COMPLETO (
  input  A,
  input  B,
  input  Cin,
  output S,
  output Cout
);

  wire meio_somador_1_cout, meio_somador_1_s, meio_somador_2_cout;

  MEIO_SOMADOR meio_somador_1 (.A(A), .B(B), .S(meio_somador_1_s), .Cout(meio_somador_1_cout));
  MEIO_SOMADOR meio_somador_2 (.A(meio_somador_1_s), .B(Cin), .S(S), .Cout(meio_somador_2_cout));
  or or_1 (Cout, meio_somador_2_cout, meio_somador_1_cout);
endmodule

module SUBTRATOR_COMPLETO (
  input  A,
  input  B,
  input  Tin,
  output S,
  output Tout
);

  wire meio_subtrator_1_s, meio_subtrator_1_tout, meio_subtrator_2_tout;

  MEIO_SUBTRATOR meio_subtrator_1 (.A(A), .B(B), .S(meio_subtrator_1_s), .Tout(meio_subtrator_1_tout));
  MEIO_SUBTRATOR meio_subtrator_2 (.A(meio_subtrator_1_s), .B(Tin), .S(S), .Tout(meio_subtrator_2_tout));
  or or_1 (Tout, meio_subtrator_2_tout, meio_subtrator_1_tout);
endmodule

module SUBTRATOR_8BITS (
  input  [7:0] A,
  input  [7:0] B,
  input  Cin,
  input  Cout,
  output [7:0] S
);

  wire multiplexer_1_out, multiplexer_2_out, multiplexer_3_out, multiplexer_4_out, multiplexer_5_out,
       multiplexer_6_out, multiplexer_7_out, multiplexer_8_out, not_1_out, not_2_out, not_3_out, not_4_out,
       not_5_out, not_6_out, not_7_out, not_8_out, somador_completo_2_cout, somador_completo_3_cout,
       somador_completo_4_cout, somador_completo_5_cout, somador_completo_6_cout, somador_completo_7_cout,
       somador_completo_8_cout;

  not not_1 (not_1_out, B[7]);
  Multiplexer #(.enable("false")) multiplexer_1 (.in0(B[7]), .in1(not_1_out), .out(multiplexer_1_out), .sel(Cin));
  SOMADOR_COMPLETO somador_completo_1 (
    .Cout(Cout), .S(S[7]), .Cin(somador_completo_2_cout), .B(multiplexer_1_out), .A(A[7]));
  not not_2 (not_2_out, B[6]);
  Multiplexer #(.enable("false")) multiplexer_2 (.in0(B[6]), .in1(not_2_out), .out(multiplexer_2_out), .sel(Cin));
  SOMADOR_COMPLETO somador_completo_2 (
    .Cout(somador_completo_2_cout), .S(S[6]), .Cin(somador_completo_3_cout), .B(multiplexer_2_out), .A(A[6]));
  Multiplexer #(.enable("false")) multiplexer_3 (.in0(B[5]), .in1(not_3_out), .out(multiplexer_3_out), .sel(Cin));
  not not_3 (not_3_out, B[5]);
  SOMADOR_COMPLETO somador_completo_3 (
    .Cout(somador_completo_3_cout), .S(S[5]), .Cin(somador_completo_4_cout), .B(multiplexer_3_out), .A(A[5]));
  not not_4 (not_4_out, B[4]);
  Multiplexer #(.enable("false")) multiplexer_4 (.in0(B[4]), .in1(not_4_out), .out(multiplexer_4_out), .sel(Cin));
  SOMADOR_COMPLETO somador_completo_4 (
    .Cout(somador_completo_4_cout), .S(S[4]), .Cin(somador_completo_5_cout), .B(multiplexer_4_out), .A(A[4]));
  not not_5 (not_5_out, B[3]);
  Multiplexer #(.enable("false")) multiplexer_5 (.in0(B[3]), .in1(not_5_out), .out(multiplexer_5_out), .sel(Cin));
  SOMADOR_COMPLETO somador_completo_5 (
    .Cout(somador_completo_5_cout), .S(S[3]), .Cin(somador_completo_6_cout), .B(multiplexer_5_out), .A(A[3]));
  not not_6 (not_6_out, B[2]);
  Multiplexer #(.enable("false")) multiplexer_6 (.in0(B[2]), .in1(not_6_out), .out(multiplexer_6_out), .sel(Cin));
  SOMADOR_COMPLETO somador_completo_6 (
    .Cout(somador_completo_6_cout), .S(S[2]), .Cin(somador_completo_7_cout), .B(multiplexer_6_out), .A(A[2]));
  not not_7 (not_7_out, B[1]);
  Multiplexer #(.enable("false")) multiplexer_7 (.in0(B[1]), .in1(not_7_out), .out(multiplexer_7_out), .sel(Cin));
  SOMADOR_COMPLETO somador_completo_7 (
    .Cout(somador_completo_7_cout), .S(S[1]), .Cin(somador_completo_8_cout), .B(multiplexer_7_out), .A(A[1]));
  not not_8 (not_8_out, B[0]);
  Multiplexer #(.enable("false")) multiplexer_8 (.in0(B[0]), .in1(not_8_out), .out(multiplexer_8_out), .sel(Cin));
  SOMADOR_COMPLETO somador_completo_8 (
    .Cout(somador_completo_8_cout), .S(S[0]), .Cin(Cin), .B(multiplexer_8_out), .A(A[0]));
endmodule

module SOMADOR_8BITS (
  input  [7:0] A,
  input  [7:0] B,
  input  Cin,
  input  Cout,
  output [7:0] S
);

  wire somador_completo_2_cout, somador_completo_3_cout, somador_completo_4_cout, somador_completo_5_cout,
       somador_completo_6_cout, somador_completo_7_cout, somador_completo_8_cout;

  SOMADOR_COMPLETO somador_completo_1 (.Cout(Cout), .S(S[7]), .Cin(somador_completo_2_cout), .B(B[7]), .A(A[7]));
  SOMADOR_COMPLETO somador_completo_2 (
    .Cout(somador_completo_2_cout), .S(S[6]), .Cin(somador_completo_3_cout), .B(B[6]), .A(A[6]));
  SOMADOR_COMPLETO somador_completo_3 (
    .Cout(somador_completo_3_cout), .S(S[5]), .Cin(somador_completo_4_cout), .B(B[5]), .A(A[5]));
  SOMADOR_COMPLETO somador_completo_4 (
    .Cout(somador_completo_4_cout), .S(S[4]), .Cin(somador_completo_5_cout), .B(B[4]), .A(A[4]));
  SOMADOR_COMPLETO somador_completo_5 (
    .Cout(somador_completo_5_cout), .S(S[3]), .Cin(somador_completo_6_cout), .B(B[3]), .A(A[3]));
  SOMADOR_COMPLETO somador_completo_6 (
    .Cout(somador_completo_6_cout), .S(S[2]), .Cin(somador_completo_7_cout), .B(B[2]), .A(A[2]));
  SOMADOR_COMPLETO somador_completo_7 (
    .Cout(somador_completo_7_cout), .S(S[1]), .Cin(somador_completo_8_cout), .B(B[1]), .A(A[1]));
  SOMADOR_COMPLETO somador_completo_8 (.Cout(somador_completo_8_cout), .S(S[0]), .Cin(Cin), .B(B[0]), .A(A[0]));
endmodule
