// Logisim project PROJETO2.circ as structural Verilog: 1 circuit, main circuit main
module main (
  input  in_1,
  input  [3:0] in_2,
  output [31:0] out_3,
  output [31:0] out_4
);

  wire ALU_SRC, AND_out, CLK, Funct_AND, MEM_R, MEM_TO_REG, or_1_out, REG_W, SB_out;
  wire [4:0] multiplexer_1_out;
  wire [31:0] adder_1_out, bit_extender_1_out, mips_alu_1_p4, mips_ram_1_p7, multiplexer_2_out, register_1_q,
       registerfile_1_p1, registerfile_1_p8;

  Adder #(.width(32)) adder_1 (.a(register_1_q), .b(32'h4), .out(adder_1_out));  // open: cin, cout
  Register #(.width(32)) register_1 (.D(adder_1_out), .Q(register_1_q), .clk(CLK));  // open: en, clr
  and AND (AND_out, ~out_3[31], ~out_3[30], ~out_3[29], ~out_3[28], ~out_3[27], ~out_3[26]);  // AND_Gate
  and SB (SB_out, out_3[31], ~out_3[30], out_3[29], ~out_3[28], ~out_3[27], ~out_3[26]);  // AND_Gate
  and and_2 (REG_W, Funct_AND, AND_out);
  and and_3 (ALU_SRC, SB_out, ~REG_W);  // AND_Gate
  or or_1 (or_1_out, SB_out, REG_W);
  // MIPSProgramROM mipsprogramrom_1: pin names not known; wires that end beside it: register_1_q, out_3
  not not_1 (MEM_R, or_1_out);
  not not_2 (MEM_TO_REG, or_1_out);
  Multiplexer #(.width(5)) multiplexer_1 (
    .in0(out_3[15:11]), .in1(out_3[20:16]), .out(multiplexer_1_out), .sel(ALU_SRC));  // open: en
  and and_4 (Funct_AND, out_3[5], ~out_3[4], ~out_3[3], out_3[2], ~out_3[1], ~out_3[0]);  // AND_Gate
  assign bit_extender_1_out = {{16{1'b0}}, out_3[15:0]};  // Bit_Extender bit_extender_1
  // RegisterFile registerfile_1: pin names not known; wires that end beside it: registerfile_1_p1, CLK, REG_W, multiplexer_1_out, out_3[25:21], out_3[20:16], out_4, registerfile_1_p8
  Clock clock_1 (.out(CLK));
  Multiplexer #(.width(32)) multiplexer_2 (
    .in0(registerfile_1_p8), .in1(bit_extender_1_out), .out(multiplexer_2_out), .sel(ALU_SRC));  // open: en
  // Mips_ALU mips_alu_1: pin names not known; wires that end beside it: out_4, multiplexer_2_out, in_2, mips_alu_1_p4
  // MIPS_RAM mips_ram_1: pin names not known; wires that end beside it: mips_alu_1_p4[19:0], registerfile_1_p8, ALU_SRC, CLK, MEM_R, in_1, mips_ram_1_p7
  Multiplexer #(.width(32)) multiplexer_3 (
    .in0(mips_alu_1_p4), .in1(mips_ram_1_p7), .out(registerfile_1_p1), .sel(MEM_TO_REG));  // open: en

  // Other names for the same wires on the sheet: ALU_OP[3:0] = in_2; Funct[5:0] = out_3[5:0];
  //   OPCODE[5:0] = out_3[31:26]; MEM_W = ALU_SRC; REG_DEST = ALU_SRC; RESET = in_1

  // Notes on the sheet:
  //   000000
  //   MEMÓRIA DE PROGRAMA
  //   101000
  //   R
  //   I
  //   0 1
  //   1 0 
  //   0 1
  //   0 1
  //   0 0
  //   0 0
  //   100100
  //   WRITE REG.
  //   Dado a ser gravado
  //   Clock
  //   Habilita a gravação
  //   End. a ser gravado
  //   Primeiro end. a ser lido
  //   Segundo end. a ser lido
  //   R
  //   I
  //   1000 (AND)
  //   0010 (SOMA)
  //   SAÍDA DE UMA OPERAÇÃO R OU I
  //   SAÍDA DE UMA OPERAÇÃO LOAD
endmodule
